// Logisim project 1001.circ as structural Verilog: 1 circuit, main circuit main
module main (
  input  in_1,
  output out_2
);

  wire and_1_out, and_2_out, button_1_out, clock_1_out, clock_2_out, D1_q, D1_qn, D2_q, D2_qn, not_1_out,
       or_1_out, x;
  wire [3:0] counter_1_q;

  BitSelector #(.width(14), .group(1)) bitselector_1 (.in(14'ha4a), .out(x), .sel(counter_1_q));
  Counter #(.width(4), .max('hf), .ongoal("wrap"), .trigger("rising"), .behavior("new")) counter_1 (
    .Q(counter_1_q), .clk(clock_1_out), .clr(button_1_out));  // open: load, D, count, carry, preset, down
  Clock #(.highDuration(1), .lowDuration(1)) clock_1 (.out(clock_1_out));
  Button button_1 (.out(button_1_out));
  Clock #(.highDuration(1), .lowDuration(1)) clock_2 (.out(clock_2_out));
  or or_1 (or_1_out, and_1_out, in_1);
  D_Flip_Flop #(.trigger("rising"), .Pre_Clr_Positions("ABOVE_BELOW"), .NegatePresetClear("false"), .enable("false"), .NewFFLayout("true")) D2 (
    .clk(clock_2_out), .D(or_1_out), .Q(D2_q), .Qn(D2_qn));  // open: preset, reset
  and and_1 (and_1_out, D2_q, D1_qn);
  and and_2 (and_2_out, D2_q, not_1_out);
  not not_1 (not_1_out, in_1);
  D_Flip_Flop #(.trigger("rising"), .Pre_Clr_Positions("ABOVE_BELOW"), .NegatePresetClear("false"), .enable("false"), .NewFFLayout("true")) D1 (
    .clk(clock_2_out), .D(and_2_out), .Q(D1_q), .Qn(D1_qn));  // open: preset, reset
  and and_3 (out_2, D1_q, D2_qn, in_1);
endmodule
